# Fritzing sketch Sketch (saved by Fritzing 0.9.3b)
breadboards: 1

parts:
  Part2 = Arduino Uno (Rev3) - ICSP
  J1 = Piezo Speaker
  R1 = Resistor [tolerance=±5% resistance=220 package="0805 [SMD]"]

nets:
  N1: Part2.D7, R1.Pin_1
  N2: Part2.GND, J1.pin1
  N3: J1.pin2, R1.Pin_0
